# Fritzing sketch breadboardLayout (saved by Fritzing 0.9.1b)
breadboards: 1

parts:
  Part1 = Arduino Uno (Rev3)
  VCC1 = Battery block 9V
  J1 = female pin header, 6 pins [form="♀ (female)"]
  M2 = DC Motor
  U4 = TOUCH [package=touch1]
  J3 = female pin header, 4 pins [form="♀ (female)"]
  R2 = Slide Potentiometer [maximum_resistance=100kΩ]
  U5 = Packages: [package=dil28-3]
  U6 = Packages: [package=dil28-3]
  U7 = Packages: [package=dil28-3]
  R7 = Resistor [tolerance=±5% resistance=10k package=THT]
  R8 = Resistor [tolerance=±5% resistance=2k package=THT]
  R9 = Resistor [tolerance=±5% resistance=2k package=THT]
  R10 = Resistor [tolerance=±5% resistance=2k package=THT]
  IC3 = H-Bridge [package=THT]
  LED9 = RGB LED (com. cathode, rbg) [package="5 mm [THT]"]

nets:
  N1: Part1.D9_PWM, U5.XLAT, U6.XLAT, U7.XLAT
  N2: Part1.D10_PWM/SS, U5.BLANK, U6.BLANK, U7.BLANK, R7.Pin_0
  N3: Part1.D11_PWM/MOSI, U6.SIN
  N4: Part1.D13/SCK, U5.SCLK, U6.SCLK, U7.SCLK
  GND: Part1.GND, VCC1.-, U5.GND, U5.VPRG, U6.GND, U6.VPRG, U7.GND, R8.Pin_1, R9.Pin_1, R10.Pin_1, IC3.GND1, IC3.GND2, IC3.GND3, IC3.GND4
  N5: Part1.D3_PWM, U5.GSCLK, U6.GSCLK, U7.GSCLK
  VCC: Part1.5V, U5.DCPRG, U5.VCC, U6.DCPRG, U6.VCC, U7.DCPRG, U7.VCC, R7.Pin_1, IC3.VCC1
  N6: VCC1.+, IC3.VCC2
  N7: J1.pin1, M2.pin_1
  N8: J1.pin2, M2.pin_2
  N9: J1.pin3, U4.T2
  N10: J1.pin4, R2.leg1
  N11: J1.pin5, R2.wiper
  N12: J1.pin6, R2.leg2
  N13: J3.pin1, LED9.red_anode
  N14: J3.pin2, LED9.common_cathode
  N15: J3.pin3, LED9.blue_anode
  N16: J3.pin4, LED9.green_anode
  N17: U5.SOUT, U7.SIN
  N18: U5.IREF, R9.Pin_0
  N19: U5.SIN, U6.SOUT
  N20: U6.OUT1, IC3.1_2EN
  N21: U6.IREF, R10.Pin_0
  N22: U6.OUT0, IC3.3_4EN
  N23: U7.IREF, R8.Pin_0
