# Fritzing sketch prototype3Layout (saved by Fritzing 0.9.1b)
breadboards: 2

parts:
  Part1 = Arduino Mega 2560 (Rev3)
  IC1 = H-Bridge [package=THT]
  IC2 = H-Bridge [package=THT]
  IC3 = H-Bridge [package=THT]
  IC4 = H-Bridge [package=THT]
  IC5 = H-Bridge [package=THT]
  BAT1 = BC9VPC [package=bc9vpc]
  J1 = female pin header, 10 pins [form="♀ (female)"]
  J2 = female pin header, 10 pins [form="♀ (female)"]
  J3 = female pin header, 10 pins [form="♀ (female)"]
  J4 = female pin header, 10 pins [form="♀ (female)"]
  J5 = female pin header, 10 pins [form="♀ (female)"]
  J6 = female pin header, 10 pins [form="♀ (female)"]
  J7 = female pin header, 10 pins [form="♀ (female)"]
  J8 = female pin header, 10 pins [form="♀ (female)"]
  J9 = female pin header, 10 pins [form="♀ (female)"]
  R1 = Resistor [tolerance=±5% resistance=220 package="0805 [SMD]"]
  R2 = Resistor [tolerance=±5% resistance=220 package="0805 [SMD]"]
  R3 = Resistor [tolerance=±5% resistance=220 package="0805 [SMD]"]
  R4 = Resistor [tolerance=±5% resistance=220 package="0805 [SMD]"]
  R5 = Resistor [tolerance=±5% resistance=220 package="0805 [SMD]"]
  R6 = Resistor [tolerance=±5% resistance=220 package="0805 [SMD]"]
  R7 = Resistor [tolerance=±5% resistance=10M package="0805 [SMD]"]
  R8 = Resistor [tolerance=±5% resistance=10M package="0805 [SMD]"]
  R9 = Resistor [tolerance=±5% resistance=10M package="0805 [SMD]"]
  R10 = Resistor [tolerance=±5% resistance=10M package="0805 [SMD]"]
  R11 = Resistor [tolerance=±5% resistance=10M package="0805 [SMD]"]
  R12 = Resistor [tolerance=±5% resistance=10M package="0805 [SMD]"]
  R13 = Resistor [tolerance=±5% resistance=10M package="0805 [SMD]"]
  R14 = Resistor [tolerance=±5% resistance=10M package="0805 [SMD]"]
  R15 = Resistor [tolerance=±5% resistance=10M package="0805 [SMD]"]

nets:
  N1: Part1.A8, J9.pin1
  N2: Part1.A9, J4.pin9, J7.pin9
  N3: Part1.A10, J2.pin9, J5.pin9
  N4: Part1.A11, J9.pin9
  N5: Part1.A12, J3.pin9, J8.pin9
  N6: Part1.A13, J1.pin9, J6.pin9
  N7: Part1.A0, J4.pin1
  N8: Part1.A1, J2.pin1
  N9: Part1.A2, J3.pin1
  N10: Part1.A3, J1.pin1
  N11: Part1.A4, J8.pin1
  N12: Part1.A5, J6.pin1
  N13: Part1.A6, J5.pin1
  N14: Part1.A7, J7.pin1
  GND1: Part1.GND, IC1.GND1, IC1.GND2, IC1.3A, IC1.3Y, IC2.GND1, IC2.GND2, IC2.GND3, IC2.GND4, IC3.GND1, IC3.GND2, IC3.GND3, IC3.GND4, IC4.GND1, IC4.GND2, IC4.GND3, IC4.GND4, IC5.GND1, IC5.GND2, IC5.GND3, IC5.GND4, BAT1.V-, J1.pin2, J2.pin2, J3.pin2, J4.pin2, J5.pin2, J6.pin2, J7.pin2, J8.pin2, J9.pin2
  N15: Part1.D13_PWM, R6.Pin_0
  N16: Part1.D12_PWM, R4.Pin_1
  N17: Part1.D11_PWM, IC4.3_4EN
  N18: Part1.D10_PWM, IC3.3_4EN
  N19: Part1.D9_PWM, IC4.1_2EN
  N20: Part1.D8_PWM, IC3.1_2EN
  N21: Part1.5V, IC1.VCC1, IC2.VCC1, IC3.VCC1, IC4.VCC1, IC5.VCC1, J1.pin3, J2.pin3, J3.pin3, J4.pin3, J5.pin3, J6.pin3, J7.pin3, J8.pin3, J9.pin3
  N22: Part1.D2_PWM, IC1.1_2EN
  N23: Part1.D3_PWM, IC2.1_2EN
  N24: Part1.D4_PWM, R5.Pin_0
  N25: Part1.D5_PWM, IC5.1_2EN
  N26: Part1.D6_PWM, IC2.3_4EN
  N27: Part1.D7_PWM, IC5.3_4EN
  N28: Part1.D22, IC2.3A
  N29: Part1.D23, IC1.1A
  N30: Part1.D24, IC2.4A
  N31: Part1.D25, IC1.2A
  N32: Part1.D26, IC5.3A
  N33: Part1.D27, IC2.1A
  N34: Part1.D28, IC5.4A
  N35: Part1.D29, IC2.2A
  N36: Part1.D30, IC3.1A
  N37: Part1.D31, IC5.1A
  N38: Part1.D32, IC3.2A
  N39: Part1.D33, IC5.2A
  N40: Part1.D34, IC4.1A
  N41: Part1.D35, IC4.3A
  N42: Part1.D36, IC4.2A
  N43: Part1.D37, IC4.4A
  N44: Part1.D38, IC3.4A
  N45: Part1.D39, IC3.3A
  N46: Part1.D40, J9.pin4, R15.Pin_0
  N47: Part1.D41, R7.Pin_0, R8.Pin_0, R9.Pin_1, R10.Pin_1, R11.Pin_0, R12.Pin_0, R13.Pin_1, R14.Pin_1, R15.Pin_1
  N48: Part1.D42, J7.pin4, R14.Pin_0
  N49: Part1.D43, J5.pin4, R13.Pin_0
  N50: Part1.D44, R3.Pin_0
  N51: Part1.D45, R2.Pin_1
  N52: Part1.D46, R1.Pin_1
  N53: Part1.D47, J8.pin4, R11.Pin_1
  N54: Part1.D48, J6.pin4, R12.Pin_1
  N55: Part1.D49, J1.pin4, R9.Pin_0
  N56: Part1.D50, J3.pin4, R10.Pin_0
  N57: Part1.D51, J4.pin4, R8.Pin_1
  N58: Part1.D52, J2.pin4, R7.Pin_1
  N59: IC1.1Y, J5.pin5
  N60: IC1.2Y, J5.pin6
  N61: IC1.VCC2, IC2.VCC2, IC3.VCC2, IC4.VCC2, IC5.VCC2, BAT1.V+
  N62: IC2.1Y, J7.pin5
  N63: IC2.2Y, J7.pin6
  N64: IC2.3Y, J6.pin6
  N65: IC2.4Y, J6.pin5
  N66: IC3.1Y, J1.pin5
  N67: IC3.2Y, J1.pin6
  N68: IC3.3Y, J4.pin6
  N69: IC3.4Y, J4.pin5
  N70: IC4.1Y, J3.pin5
  N71: IC4.2Y, J3.pin6
  N72: IC4.3Y, J2.pin6
  N73: IC4.4Y, J2.pin5
  N74: IC5.1Y, J9.pin5
  N75: IC5.2Y, J9.pin6
  N76: IC5.3Y, J8.pin6
  N77: IC5.4Y, J8.pin5
  N78: J1.pin7, J2.pin7, J3.pin7, J4.pin7, R5.Pin_1
  N79: J1.pin8, J2.pin8, J3.pin8, J4.pin8, R6.Pin_1
  N80: J1.pin10, J2.pin10, J3.pin10, J4.pin10, R4.Pin_0
  N81: J5.pin7, J6.pin7, J7.pin7, J8.pin7, J9.pin7, R1.Pin_0
  N82: J5.pin8, J6.pin8, J7.pin8, J8.pin8, J9.pin8, R2.Pin_0
  N83: J5.pin10, J6.pin10, J7.pin10, J8.pin10, J9.pin10, R3.Pin_1
